// Logisim project control_logic.circ as structural Verilog
module control_logic (
  input  [31:0] inst,
  input  BrEq,
  input  BrLt,
  output [3:0] WRITE_ENABLE,
  output PCSel,
  output RegWEn,
  output [2:0] ImmSel,
  output BrUn,
  output ASel,
  output BSel,
  output [3:0] ALUSel,
  output MemRW,
  output [1:0] WBSel,
  output CSRSel,
  output CSRWen
);

  wire comparator_1_eq, comparator_2_eq, comparator_3_eq, comparator_4_eq, comparator_5_eq, comparator_6_eq,
       comparator_7_eq, comparator_8_eq, comparator_9_eq, comparator_10_eq, comparator_11_eq;
  wire [3:0] multiplexer_11_out, multiplexer_12_out, multiplexer_13_out;
  wire [16:0] b_instruction_1_out_4, csr_instruction_1_out_3, i_instruction_1_ilogicbits, multiplexer_1_out,
       multiplexer_2_out, multiplexer_3_out, multiplexer_4_out, multiplexer_5_out, multiplexer_6_out,
       multiplexer_7_out, multiplexer_8_out, multiplexer_9_out, multiplexer_10_out, r_instruction_1_out_3;

  Comparator #(.width(7)) comparator_1 (.a(inst[6:0]), .b(7'b0110011), .eq(comparator_1_eq));  // open: gt, lt
  Comparator #(.width(7)) comparator_2 (.a(inst[6:0]), .b(7'b0000011), .eq(comparator_2_eq));  // open: gt, lt
  Comparator #(.width(7)) comparator_3 (.a(inst[6:0]), .b(7'b0010011), .eq(comparator_3_eq));  // open: gt, lt
  Comparator #(.width(7)) comparator_4 (.a(inst[6:0]), .b(7'b0100011), .eq(comparator_4_eq));  // open: gt, lt
  Comparator #(.width(7)) comparator_5 (.a(inst[6:0]), .b(7'b1100011), .eq(comparator_5_eq));  // open: gt, lt
  Comparator #(.width(7)) comparator_6 (.a(inst[6:0]), .b(7'b0010111), .eq(comparator_6_eq));  // open: gt, lt
  Comparator #(.width(7)) comparator_7 (.a(inst[6:0]), .b(7'b0110111), .eq(comparator_7_eq));  // open: gt, lt
  Comparator #(.width(7)) comparator_8 (.a(inst[6:0]), .b(7'b1100111), .eq(comparator_8_eq));  // open: gt, lt
  Comparator #(.width(7)) comparator_9 (.a(inst[6:0]), .b(7'b1110011), .eq(comparator_9_eq));  // open: gt, lt
  Comparator #(.width(7)) comparator_10 (.a(inst[6:0]), .b(7'b1101111), .eq(comparator_10_eq));  // open: gt, lt
  CSR_Instruction csr_instruction_1 (.CSRAddr(inst[31:20]), .FUNC3(inst[14:12]), .out_3(csr_instruction_1_out_3));
  Multiplexer #(.enable("false"), .width(17)) multiplexer_1 (
    .in0({17{1'b0}}), .in1(17'hd7), .out(multiplexer_1_out), .sel(comparator_10_eq));
  Multiplexer #(.enable("false"), .width(17)) multiplexer_2 (
    .in0({17{1'b0}}), .in1(17'h20d2), .out(multiplexer_2_out), .sel(comparator_6_eq));
  Multiplexer #(.enable("false"), .width(17)) multiplexer_3 (
    .in0({17{1'b0}}), .in1(17'h2d92), .out(multiplexer_3_out), .sel(comparator_7_eq));
  Multiplexer #(.enable("false"), .width(17)) multiplexer_4 (
    .in0({17{1'b0}}), .in1(17'h87), .out(multiplexer_4_out), .sel(comparator_8_eq));
  Multiplexer #(.enable("false"), .width(17)) multiplexer_5 (
    .in0({17{1'b0}}), .in1(csr_instruction_1_out_3), .out(multiplexer_5_out), .sel(comparator_9_eq));
  R_Instruction r_instruction_1 (.func3(inst[14:12]), .func7(inst[31:25]), .out_3(r_instruction_1_out_3));
  I_Instruction i_instruction_1 (.func3(inst[14:12]), .Immediate(inst[31:20]), .ILogicBits(i_instruction_1_ilogicbits));
  Multiplexer #(.enable("false"), .width(17)) multiplexer_6 (
    .in0({17{1'b0}}), .in1(r_instruction_1_out_3), .out(multiplexer_6_out), .sel(comparator_1_eq));
  B_Instruction b_instruction_1 (.BrLT(BrLt), .BrEQ(BrEq), .FUNC3(inst[14:12]), .out_4(b_instruction_1_out_4));
  Multiplexer #(.enable("false"), .width(17)) multiplexer_7 (
    .in0({17{1'b0}}), .in1(17'h4086), .out(multiplexer_7_out), .sel(comparator_2_eq));
  Multiplexer #(.enable("false"), .width(17)) multiplexer_8 (
    .in0({17{1'b0}}), .in1(i_instruction_1_ilogicbits), .out(multiplexer_8_out), .sel(comparator_3_eq));
  Multiplexer #(.enable("false"), .width(17)) multiplexer_9 (
    .in0({17{1'b0}}), .in1(17'h1088), .out(multiplexer_9_out), .sel(comparator_4_eq));
  Multiplexer #(.enable("false"), .width(17)) multiplexer_10 (
    .in0({17{1'b0}}), .in1(b_instruction_1_out_4), .out(multiplexer_10_out), .sel(comparator_5_eq));
  assign {CSRWen, CSRSel, WBSel, MemRW, ALUSel, BSel, ASel, BrUn, ImmSel, RegWEn, PCSel} = multiplexer_6_out | multiplexer_7_out | multiplexer_8_out | multiplexer_9_out | multiplexer_10_out | multiplexer_2_out | multiplexer_3_out | multiplexer_4_out | multiplexer_5_out | multiplexer_1_out;  // OR_Gate or_1, 17 bits wide
  Multiplexer #(.enable("false"), .select(2), .width(4)) multiplexer_11 (
    .in0(4'b0001), .in1(4'b0010), .in2(4'b0100), .in3(4'b1000), .out(multiplexer_11_out), .sel(inst[8:7]));
  Multiplexer #(.enable("false"), .select(2), .width(4)) multiplexer_12 (
    .in0(4'b0011), .in1(4'b0110), .in2(4'b1100), .out(multiplexer_12_out), .sel(inst[8:7]));  // open: in3
  Multiplexer #(.enable("false"), .select(2), .width(4)) multiplexer_13 (
    .in0(multiplexer_11_out), .in1(multiplexer_12_out), .in2(4'b1111), .out(multiplexer_13_out),
    .sel(inst[13:12]));  // open: in3
  Multiplexer #(.enable("false"), .width(4)) multiplexer_14 (
    .in0(4'b0000), .in1(multiplexer_13_out), .out(WRITE_ENABLE), .sel(comparator_11_eq));
  Comparator #(.width(7)) comparator_11 (.a(inst[6:0]), .b(7'b0100011), .eq(comparator_11_eq));  // open: gt, lt

  // Other names for the same wires on the sheet: opcode[6:0] = inst[6:0]; WEN_bits[1:0] = inst[8:7];
  //   func3[2:0] = inst[14:12]; CSRAddr[11:0] = inst[31:20]; Immediate[11:0] = inst[31:20]; func7[6:0] = inst[31:25]

  // Notes on the sheet:
  //   INPUTS to your circuit
  //   0: PCSel, 1: RegWEn, 2-4: ImmSel, 5: BrUn, 6: Asel, 7: BSel
  //   8-11: ALUSel, 12: MemRW, 13-14: WBSel, 15: CSRSel, 16: CSRWEn
  //   DON'T CHANGE THE LOCATIONS OF THE INPUTS AND OUTPUTS!
  //   OUTPUT from your circuit
  //   FIXME: How do csr operations work??
endmodule

module I_Instruction (
  input  [2:0] func3,
  input  [11:0] Immediate,
  output [16:0] ILogicBits
);

  wire comparator_1_eq, comparator_2_eq;
  wire [3:0] multiplexer_1_out;
  wire [16:0] multiplexer_2_out, multiplexer_3_out;

  Multiplexer #(.enable("false"), .select(3), .width(4)) multiplexer_1 (
    .in0(4'b0000), .in2(4'b0111), .in4(4'b0011), .in6(4'b0010), .in7(4'b0001), .out(multiplexer_1_out),
    .sel(func3));  // open: in1, in3, in5
  Multiplexer #(.enable("false"), .width(17)) multiplexer_2 (
    .in0(17'h2482), .in1(17'h2582), .out(multiplexer_2_out), .sel(Immediate[10]));
  Comparator #(.width(3)) comparator_1 (.a(func3), .b(3'b101), .eq(comparator_1_eq));  // open: gt, lt
  Multiplexer #(.enable("false"), .width(17)) multiplexer_3 (
    .in0({5'b00010, multiplexer_1_out, 8'h86}), .in1(multiplexer_2_out), .out(multiplexer_3_out),
    .sel(comparator_1_eq));
  Comparator #(.width(3)) comparator_2 (.a(func3), .b(3'b001), .eq(comparator_2_eq));  // open: gt, lt
  Multiplexer #(.enable("false"), .width(17)) multiplexer_4 (
    .in0(multiplexer_3_out), .in1(17'h2682), .out(ILogicBits), .sel(comparator_2_eq));

  // Notes on the sheet:
  //   CURRENTLY, 3 Instructions above assume ImmSel = 0
  //   FORMAT: 0010[OP]100[000]10
  //   0: PCSel = 0, 1: RegWEn = 1, 2-4: ImmSel = 1, 5: BrUn = 0, 6: Asel = 0, 7: BSel = 1
  //   8-11: ALUSel = OPERATION, 12: MemRW = 0, 13-14: WBSel = 1, 15: CSRSel = 0, 16: CSRWEn = 0
  //   NOTE TO SELF: SLLI, SRAI, SRLI NEED TO BE ADJUSTED (THEY ARE AT THE MUXES)
endmodule

module B_Instruction (
  input  BrLT,
  input  BrEQ,
  input  [2:0] FUNC3,
  output [16:0] out_4
);

  wire not_1_out, not_2_out;

  Comparator #(.mode("unsigned"), .width(3)) comparator_1 (.a(FUNC3), .b(3'b101), .gt(out_4[5]));  // open: eq, lt
  not not_1 (not_1_out, BrEQ);
  not not_2 (not_2_out, BrLT);
  Multiplexer #(.enable("false"), .select(3)) multiplexer_1 (
    .in0(BrEQ), .in1(not_1_out), .in4(BrLT), .in5(not_2_out), .in6(BrLT), .in7(not_2_out), .out(out_4[0]),
    .sel(FUNC3));  // open: in2, in3

  assign {out_4[16:6], out_4[4:1]} = 15'h36;

  // Notes on the sheet:
  //   0: PCSel = BranchTaken, 1: RegWEn = 0, 2-4: ImmSel = 3, 5: BrUn = BranchUnsigned, 6: Asel = 1, 7: BSel = 1
  //   8-11: ALUSel = 0, 12: MemRW = 0, 13-14: WBSel = 0, 15: CSRSel = 0, 16: CSRWEn = 0
endmodule

module R_Instruction (
  input  [2:0] func3,
  input  [6:0] func7,
  output [16:0] out_3
);

  Multiplexer #(.enable("false"), .select(5), .width(4)) multiplexer_1 (
    .in0(4'b0000), .in1(4'b0110), .in2(4'b0111), .in4(4'b0011), .in5(4'b0100), .in6(4'b0010), .in7(4'b0001),
    .in8(4'b1010), .in9(4'b1110), .in11(4'b1011), .in16(4'b1100), .in21(4'b0101), .out(out_3[11:8]),
    .sel({func7[5], func7[0], func3}));  // open: in3, in10, in12, in13, in14, in15, in17, in18, in19, in20, in22, in23, in24, in25, in26, in27, in28, in29, in30, in31

  assign {out_3[16:12], out_3[7:0]} = 13'h202;

  // Notes on the sheet:
  //   NOTE: Need to account for BSel?
  //   0: PCSel = 0, 1: RegWEn = 1, 2-4: ImmSel = 0, 5: BrUn = 0, 6: Asel = 0, 7: BSel = 0
  //   8-11: ALUSel = OPERATION, 12: MemRW = 0, 13-14: WBSel = 1, 15: CSRSel = 0, 16: CSRWEn = 0
endmodule

module CSR_Instruction (
  input  [11:0] CSRAddr,
  input  [2:0] FUNC3,
  output [16:0] out_3
);

  Comparator #(.mode("unsigned"), .width(3)) comparator_1 (.a(FUNC3), .b(3'b101), .eq(out_3[15]));  // open: gt, lt
  Comparator #(.mode("unsigned"), .width(12)) comparator_2 (.a(CSRAddr), .b(12'h51e), .eq(out_3[16]));  // open: gt, lt

  assign out_3[14:0] = {15{1'b0}};

  // Other names for the same wires on the sheet: csr[11:0] = CSRAddr
endmodule
