// Logisim project cpu.circ as structural Verilog: 1 circuit, main circuit cpu
module cpu (
  input  clk,
  input  [31:0] INSTRUCTION,
  input  [31:0] READ_DATA,
  output [31:0] WRITE_ADDRESS,
  output [31:0] PROGRAM_COUNTER,
  output [31:0] ra,
  output [31:0] sp,
  output [31:0] t0,
  output [31:0] t1,
  output [31:0] t2,
  output [31:0] s0,
  output [31:0] s1,
  output [31:0] a0,
  output [31:0] tohost,
  output [3:0] WRITE_ENABLE,
  output [31:0] WRITE_DATA
);

  wire ASel, BrEq, BrLt, BrUn, BSel, comparator_1_eq, comparator_2_eq, comparator_3_eq, CSRSel, CSRWEn,
       MemRW, nop, PCSel, REGWEN;
  wire [1:0] L_lowerbits, WBSel;
  wire [2:0] func3, ImmSel;
  wire [3:0] ALUSEL;
  wire [4:0] bit_extender_2_out, multiplier_1_out;
  wire [7:0] multiplexer_10_out;
  wire [11:0] multiplexer_3_out;
  wire [15:0] multiplexer_11_out;
  wire [31:0] adder_1_out, adder_2_out, alu_1_result, and_1_out, bit_extender_1_out, INSTRUCTION_UPD, lb, lh,
       multiplexer_1_out, multiplexer_4_out, multiplexer_5_out, multiplexer_6_out, multiplexer_8_out,
       register_1_q, register_3_q, rs1, rs2, WriteBack;
  wire [31:2] imm_gen_1_imm;

  Register #(.width(32)) register_1 (.D(INSTRUCTION), .en(1'b1), .clk(clk), .Q(register_1_q));  // open: clr
  Register #(.width(1)) register_2 (.D(PCSel), .en(1'b1), .clk(clk), .Q(nop));  // open: clr
  Adder #(.width(32)) adder_1 (.a(PROGRAM_COUNTER), .b(32'h4), .out(adder_1_out));  // open: cin, cout
  Register #(.width(32)) register_3 (.D(PROGRAM_COUNTER), .en(1'b1), .clk(clk), .Q(register_3_q));  // open: clr
  Multiplexer #(.enable("false"), .width(32)) multiplexer_1 (
    .in0(adder_1_out), .in1(WRITE_ADDRESS), .out(multiplexer_1_out), .sel(PCSel));
  Multiplexer #(.enable("false"), .width(32)) multiplexer_2 (
    .in0(register_1_q), .in1(32'h13), .out({INSTRUCTION_UPD[31:15], func3, INSTRUCTION_UPD[11:0]}), .sel(nop));
  Register #(.width(32)) PC (.D(multiplexer_1_out), .en(1'b1), .clk(clk), .Q(PROGRAM_COUNTER));  // open: clr
  control_logic control_logic_1 (
    .CSRWen(CSRWEn), .WRITE_ENABLE(WRITE_ENABLE), .PCSel(PCSel), .RegWEn(REGWEN), .ImmSel(ImmSel),
    .BrUn(BrUn), .ASel(ASel), .BSel(BSel), .ALUSel(ALUSEL), .MemRW(MemRW), .WBSel(WBSel), .CSRSel(CSRSel),
    .inst({INSTRUCTION_UPD[31:15], func3, INSTRUCTION_UPD[11:0]}), .BrEq(BrEq), .BrLt(BrLt));
  imm_gen imm_gen_1 (
    .inst({INSTRUCTION_UPD[31:15], func3, INSTRUCTION_UPD[11:0]}), .ImmSel(ImmSel),
    .imm({imm_gen_1_imm, L_lowerbits}));
  regfile regfile_1 (
    .rs1(INSTRUCTION_UPD[19:15]), .rs2(INSTRUCTION_UPD[24:20]), .rd(INSTRUCTION_UPD[11:7]),
    .Write_Data(WriteBack), .RegWEn(REGWEN), .clk(clk), .ra(ra), .sp(sp), .t0(t0), .t1(t1), .t2(t2), .s0(s0),
    .s1(s1), .a0(a0), .Read_Data_1(rs1), .Read_Data_2(rs2));
  Comparator #(.mode("unsigned"), .width(12)) comparator_1 (
    .a(INSTRUCTION_UPD[31:20]), .b(12'h51e), .eq(comparator_1_eq));  // open: gt, lt
  assign bit_extender_1_out = {{27{INSTRUCTION_UPD[19]}}, INSTRUCTION_UPD[19:15]};  // Bit_Extender bit_extender_1
  Multiplexer #(.enable("false"), .width(12)) multiplexer_3 (
    .in0({12{1'b0}}), .in1(INSTRUCTION_UPD[31:20]), .out(multiplexer_3_out), .sel(comparator_1_eq));
  Multiplexer #(.enable("false"), .width(32)) multiplexer_4 (
    .in0(bit_extender_1_out), .in1(rs1), .out(multiplexer_4_out), .sel(comparator_2_eq));
  Comparator #(.mode("unsigned"), .width(3)) comparator_2 (
    .a(func3), .b(3'b001), .eq(comparator_2_eq));  // open: gt, lt
  Multiplexer #(.enable("false"), .width(32)) multiplexer_5 (
    .in0(rs1), .in1(register_3_q), .out(multiplexer_5_out), .sel(ASel));
  Multiplexer #(.enable("false"), .width(32)) multiplexer_6 (
    .in0(rs2), .in1({imm_gen_1_imm, L_lowerbits}), .out(multiplexer_6_out), .sel(BSel));
  branch_comp branch_comp_1 (.rs1(rs1), .rs2(rs2), .BrUn(BrUn), .BrEq(BrEq), .BrLt(BrLt));
  alu alu_1 (.Result(alu_1_result), .A(multiplexer_5_out), .B(multiplexer_6_out), .ALUSel(ALUSEL));
  csr csr_1 (.CSR_address(multiplexer_3_out), .CSR_din(multiplexer_4_out), .CSR_WE(CSRWEn), .clk(clk), .tohost(tohost));
  assign and_1_out = alu_1_result & 32'hfffffffe;  // AND_Gate and_1, 32 bits wide
  Comparator #(.mode("unsigned"), .width(7)) comparator_3 (
    .a(INSTRUCTION_UPD[6:0]), .b(7'b1100111), .eq(comparator_3_eq));  // open: gt, lt
  Multiplexer #(.enable("false"), .width(32)) multiplexer_7 (
    .in0(alu_1_result), .in1(and_1_out), .out(WRITE_ADDRESS), .sel(comparator_3_eq));
  Adder #(.width(32)) adder_2 (.a(register_3_q), .b(32'h4), .out(adder_2_out));  // open: cin, cout
  Multiplexer #(.enable("false"), .select(3), .width(32)) multiplexer_8 (
    .in0(lb), .in1(lh), .in2(READ_DATA), .out(multiplexer_8_out), .sel(func3));  // open: in3, in4, in5, in6, in7
  Multiplexer #(.enable("false"), .select(2), .width(32)) multiplexer_9 (
    .in0(adder_2_out), .in1(WRITE_ADDRESS), .in2(multiplexer_8_out), .out(WriteBack), .sel(WBSel));  // open: in3
  assign bit_extender_2_out = {{3{L_lowerbits[1]}}, L_lowerbits};  // Bit_Extender bit_extender_2
  Multiplier #(.width(5)) multiplier_1 (
    .a(bit_extender_2_out), .b(5'b01000), .out(multiplier_1_out));  // open: cin, cout
  Multiplexer #(.enable("false"), .select(2), .width(8)) multiplexer_10 (
    .in0(READ_DATA[7:0]), .in1(READ_DATA[15:8]), .in2(READ_DATA[23:16]), .in3(READ_DATA[31:24]),
    .out(multiplexer_10_out), .sel(L_lowerbits));
  Multiplexer #(.enable("false"), .select(2), .width(16)) multiplexer_11 (
    .in0(READ_DATA[15:0]), .in1(READ_DATA[23:8]), .in2(READ_DATA[31:16]), .out(multiplexer_11_out),
    .sel(L_lowerbits));  // open: in3
  Shifter #(.shift("rl"), .width(32)) shifter_1 (.in(rs2), .\dist (multiplier_1_out), .out(WRITE_DATA));
  assign lb = {{24{multiplexer_10_out[7]}}, multiplexer_10_out};  // Bit_Extender bit_extender_3
  assign lh = {{16{multiplexer_11_out[15]}}, multiplexer_11_out};  // Bit_Extender bit_extender_4

  // Other names for the same wires on the sheet: fromALU[31:0] = WRITE_ADDRESS; opcode[6:0] = INSTRUCTION_UPD[6:0];
  //   INSTRUCTION_UPD[14:12] = func3; WRITE_DATA_SRC[31:0] = rs2; toAsel[31:0] = PROGRAM_COUNTER

  // Notes on the sheet:
  //   Output to IMEM
  //   IMEM (do **NOT** move this)
  //   Inputs from IMEM
  //   Inputs/Outputs for testing. Do **NOT** move these.
  //   Need to figure out how to wire RS1 and RS2
  //   Outputs To DMEM
  //   DMEM (do **NOT** move this)
  //   Inputs From DMEM
endmodule
