// Logisim project imm_gen.circ as structural Verilog: 1 circuit, main circuit imm_gen
module imm_gen (
  input  [31:0] inst,
  input  [2:0] ImmSel,
  output [31:0] imm
);

  wire [31:0] B, I, J, S;

  Multiplexer #(.enable("false"), .select(5), .width(32)) multiplexer_1 (
    .in0(I), .in4(I), .in5({inst[31:12], {12{1'b0}}}), .in6(I), .in8(S), .in13({inst[31:12], {12{1'b0}}}),
    .in24(B), .in25(I), .in27(J), .out(imm), .sel(inst[6:2]));  // open: in1, in2, in3, in7, in9, in10, in11, in12, in14, in15, in16, in17, in18, in19, in20, in21, in22, in23, in26, in28, in29, in30, in31
  assign J = {{11{inst[31]}}, {inst[31], inst[19:12], inst[20], inst[30:21], 1'b0}};  // Bit_Extender bit_extender_1
  assign B = {{19{inst[31]}}, {inst[31], inst[7], inst[30:25], inst[11:8], 1'b0}};  // Bit_Extender bit_extender_2
  assign I = {{20{inst[31]}}, inst[31:20]};  // Bit_Extender bit_extender_3
  assign S = {{20{inst[31]}}, {inst[31:25], inst[11:7]}};  // Bit_Extender bit_extender_4

  // Other names for the same wires on the sheet: func3[2:0] = inst[14:12]; U[31:12] = inst[31:12];
  //   rs1[4:0] = inst[19:15]; rs2[4:0] = inst[24:20]; rd[4:0] = inst[11:7]; func7[6:0] = inst[31:25];
  //   opcode[4:0] = inst[6:2]

  // Notes on the sheet:
  //   INPUTS to your circuit
  //   DON'T CHANGE THE LOCATIONS OF THE INPUTS AND OUTPUTS!
  //   OUTPUT from your circuit
endmodule
