// Logisim project regfile.circ as structural Verilog: 1 circuit, main circuit regfile
module regfile (
  input  [4:0] rs1,
  input  [4:0] rs2,
  input  [4:0] rd,
  input  [31:0] Write_Data,
  input  RegWEn,
  input  clk,
  output [31:0] ra,
  output [31:0] sp,
  output [31:0] t0,
  output [31:0] t1,
  output [31:0] t2,
  output [31:0] s0,
  output [31:0] s1,
  output [31:0] a0,
  output [31:0] Read_Data_1,
  output [31:0] Read_Data_2
);

  wire x0_WE, x1_WE, x2_WE, x3_WE, x4_WE, x5_WE, x6_WE, x7_WE, x8_WE, x9_WE, x10_WE, x11_WE, x12_WE, x13_WE,
       x14_WE, x15_WE, x16_WE, x17_WE, x18_WE, x19_WE, x20_WE, x21_WE, x22_WE, x23_WE, x24_WE, x25_WE,
       x26_WE, x27_WE, x28_WE, x29_WE, x30_WE, x31_WE;
  wire [31:0] x3, x4, x11, x12, x13, x14, x15, x16, x17, x18, x19, x20, x21, x22, x23, x24, x25, x26, x27,
       x28, x29, x30, x31, zero;

  Demultiplexer #(.enable("false"), .select(5)) demultiplexer_1 (
    .out0(x0_WE), .out1(x1_WE), .out2(x2_WE), .out3(x3_WE), .out4(x4_WE), .out5(x5_WE), .out6(x6_WE),
    .out7(x7_WE), .out8(x8_WE), .out9(x9_WE), .out10(x10_WE), .out11(x11_WE), .out12(x12_WE), .out13(x13_WE),
    .out14(x14_WE), .out15(x15_WE), .out16(x16_WE), .out17(x17_WE), .out18(x18_WE), .out19(x19_WE),
    .out20(x20_WE), .out21(x21_WE), .out22(x22_WE), .out23(x23_WE), .out24(x24_WE), .out25(x25_WE),
    .out26(x26_WE), .out27(x27_WE), .out28(x28_WE), .out29(x29_WE), .out30(x30_WE), .out31(x31_WE),
    .in(RegWEn), .sel(rd));
  Register #(.width(32)) x0 (.D(Write_Data), .en(x0_WE), .clk(clk), .Q(zero), .clr(1'b1));
  Register #(.width(32)) x1 (.D(Write_Data), .en(x1_WE), .clk(clk), .Q(ra));  // open: clr
  Register #(.width(32)) x2 (.D(Write_Data), .en(x2_WE), .clk(clk), .Q(sp));  // open: clr
  Register #(.width(32)) u_x3 (.D(Write_Data), .en(x3_WE), .clk(clk), .Q(x3));  // open: clr
  Register #(.width(32)) u_x16 (.D(Write_Data), .en(x16_WE), .clk(clk), .Q(x16));  // open: clr
  Register #(.width(32)) u_x17 (.D(Write_Data), .en(x17_WE), .clk(clk), .Q(x17));  // open: clr
  Register #(.width(32)) u_x18 (.D(Write_Data), .en(x18_WE), .clk(clk), .Q(x18));  // open: clr
  Register #(.width(32)) u_x19 (.D(Write_Data), .en(x19_WE), .clk(clk), .Q(x19));  // open: clr
  Register #(.width(32)) u_x4 (.D(Write_Data), .en(x4_WE), .clk(clk), .Q(x4));  // open: clr
  Register #(.width(32)) x5 (.D(Write_Data), .en(x5_WE), .clk(clk), .Q(t0));  // open: clr
  Register #(.width(32)) x6 (.D(Write_Data), .en(x6_WE), .clk(clk), .Q(t1));  // open: clr
  Register #(.width(32)) x7 (.D(Write_Data), .en(x7_WE), .clk(clk), .Q(t2));  // open: clr
  Register #(.width(32)) u_x20 (.D(Write_Data), .en(x20_WE), .clk(clk), .Q(x20));  // open: clr
  Register #(.width(32)) u_x21 (.D(Write_Data), .en(x21_WE), .clk(clk), .Q(x21));  // open: clr
  Register #(.width(32)) u_x22 (.D(Write_Data), .en(x22_WE), .clk(clk), .Q(x22));  // open: clr
  Register #(.width(32)) u_x23 (.D(Write_Data), .en(x23_WE), .clk(clk), .Q(x23));  // open: clr
  Register #(.width(32)) x8 (.D(Write_Data), .en(x8_WE), .clk(clk), .Q(s0));  // open: clr
  Register #(.width(32)) x9 (.D(Write_Data), .en(x9_WE), .clk(clk), .Q(s1));  // open: clr
  Register #(.width(32)) x10 (.D(Write_Data), .en(x10_WE), .clk(clk), .Q(a0));  // open: clr
  Register #(.width(32)) u_x11 (.D(Write_Data), .en(x11_WE), .clk(clk), .Q(x11));  // open: clr
  Register #(.width(32)) u_x24 (.D(Write_Data), .en(x24_WE), .clk(clk), .Q(x24));  // open: clr
  Register #(.width(32)) u_x25 (.D(Write_Data), .en(x25_WE), .clk(clk), .Q(x25));  // open: clr
  Register #(.width(32)) u_x26 (.D(Write_Data), .en(x26_WE), .clk(clk), .Q(x26));  // open: clr
  Register #(.width(32)) u_x27 (.D(Write_Data), .en(x27_WE), .clk(clk), .Q(x27));  // open: clr
  Register #(.width(32)) u_x12 (.D(Write_Data), .en(x12_WE), .clk(clk), .Q(x12));  // open: clr
  Register #(.width(32)) u_x13 (.D(Write_Data), .en(x13_WE), .clk(clk), .Q(x13));  // open: clr
  Register #(.width(32)) u_x14 (.D(Write_Data), .en(x14_WE), .clk(clk), .Q(x14));  // open: clr
  Register #(.width(32)) u_x15 (.D(Write_Data), .en(x15_WE), .clk(clk), .Q(x15));  // open: clr
  Register #(.width(32)) u_x28 (.D(Write_Data), .en(x28_WE), .clk(clk), .Q(x28));  // open: clr
  Register #(.width(32)) u_x29 (.D(Write_Data), .en(x29_WE), .clk(clk), .Q(x29));  // open: clr
  Register #(.width(32)) u_x30 (.D(Write_Data), .en(x30_WE), .clk(clk), .Q(x30));  // open: clr
  Register #(.width(32)) u_x31 (.D(Write_Data), .en(x31_WE), .clk(clk), .Q(x31));  // open: clr
  Multiplexer #(.enable("false"), .select(5), .width(32)) multiplexer_1 (
    .in0(zero), .in1(ra), .in2(sp), .in3(x3), .in4(x4), .in5(t0), .in6(t1), .in7(t2), .in8(s0), .in9(s1),
    .in10(a0), .in11(x11), .in12(x12), .in13(x13), .in14(x14), .in15(x15), .in16(x16), .in17(x17),
    .in18(x18), .in19(x19), .in20(x20), .in21(x21), .in22(x22), .in23(x23), .in24(x24), .in25(x25),
    .in26(x26), .in27(x27), .in28(x28), .in29(x29), .in30(x30), .in31(x31), .out(Read_Data_1), .sel(rs1));
  Multiplexer #(.enable("false"), .select(5), .width(32)) multiplexer_2 (
    .in0(zero), .in1(ra), .in2(sp), .in3(x3), .in4(x4), .in5(t0), .in6(t1), .in7(t2), .in8(s0), .in9(s1),
    .in10(a0), .in11(x11), .in12(x12), .in13(x13), .in14(x14), .in15(x15), .in16(x16), .in17(x17),
    .in18(x18), .in19(x19), .in20(x20), .in21(x21), .in22(x22), .in23(x23), .in24(x24), .in25(x25),
    .in26(x26), .in27(x27), .in28(x28), .in29(x29), .in30(x30), .in31(x31), .out(Read_Data_2), .sel(rs2));

  // Other names for the same wires on the sheet: read_data1[31:0] = Read_Data_1; read_data2[31:0] = Read_Data_2;
  //   read_reg1[4:0] = rs1; read_reg2[4:0] = rs2; write_en = RegWEn; write_reg[4:0] = rd

  // Notes on the sheet:
  //   INPUTS to your circuit
  //   DON'T CHANGE THE LOCATIONS OF THE INPUTS AND OUTPUTS!
  //   These are DEBUG/TEST outputs from your circuit.
  //   OUTPUTS from your circuit
endmodule
