// Logisim project cpu-reg_cover3.circ as structural Verilog: 1 circuit, main circuit run_main
module run_main (
  output [31:0] ra,
  output [31:0] sp,
  output [31:0] t0,
  output [31:0] t1,
  output [31:0] t2,
  output [31:0] s0,
  output [31:0] s1,
  output [31:0] a0,
  output [31:0] Requested_Address,
  output [31:0] Requested_Instruction,
  output [15:0] Time_Step,
  output halt
);

  wire clk;

  Clock clock_1 (.out(clk));
  // Probe on Requested_Address
  // test_harness test_harness_1: pin names not known; wires that end beside it: Requested_Instruction, clk, Requested_Address, ra, sp, t0, t1, t2, s0, s1, a0
  ROM #(.addrWidth(14), .dataWidth(32)) rom_1 (.addr(Requested_Address[15:2]), .data(Requested_Instruction));
  // Probe on Requested_Instruction
  Counter #(.max('hffff), .width(16)) counter_1 (.clk(clk), .Q(Time_Step));  // open: clr, load, up, count, D, carry
  Comparator #(.width(16)) comparator_1 (.a(Time_Step), .b(16'h25), .eq(halt));  // open: gt, lt

  // Other names for the same wires on the sheet: fetch_addr[31:0] = Requested_Address;
  //   Instruction[31:0] = Requested_Instruction

  // Notes on the sheet:
  //   contents of rom_1 (hex, n*v repeats v):
  //   00100013 00100093 00100113 00100193 00100213 00100293 00100313 00100393 00100413 00100493 00100513
  //   00100593 00100613 00100693 00100713 00100793 00100813 00100893 00100913 00100993 00100A13 00100A93
  //   00100B13 00100B93 00100C13 00100C93 00100D13 00100D93 00100E13 00100E93 00100F13 00100F93 001F8F93
  //   001F0F13 001E8E93
  //   Instruction Memory
  //   Halts Execution After Constant # of Clock Cycles
  //   Constant
endmodule
